# Fritzing sketch estacao-meteorologica-1 (saved by Fritzing 0.9.10b)

parts:
  U1 = ESP32-38PinWide [part_number=ESP32-38PinWide]
  M1 = NEO-6M GPS Module [part_number=GY-GPS6MV2]
  R1 = Resistor [tolerance=±5% power=0.25 resistance=220 package=THT]
  R2 = Resistor [tolerance=±5% power=0.25 resistance=220 package=THT]
  R3 = Resistor [tolerance=±5% power=0.25 resistance=220 package=THT]
  LED1 = RGB LED (com. cathode, rgb) [package="5 mm [THT]"]
  Componente2 = BH1750
  OLED_I2C1 = OLED 128x64 I2C Monochrome Display
  M2 = BME280
  DHT1 = DHT22 Humidity and Temperature Sensor

nets:
  N1: U1.3.3, M2.VIN
  N2: U1.GPIO33, R2.Pin_0
  N3: U1.GPIO12, R3.Pin_0
  GND: U1.GND, M1.GND, LED1.common_cathode, Componente2.GND, OLED_I2C1.GND, M2.GND, DHT1.GND
  N4: U1.GPIO13, R1.Pin_0
  VCC: U1.VIN, M1.Vcc, Componente2.VCC, OLED_I2C1.VDD, DHT1.VDD
  N5: U1.GPIO16, M1.Tx
  N6: U1.GPIO17, M1.Rx
  N7: U1.GPIO18, DHT1.DATA
  N8: U1.GPIO21, Componente2.SDA, OLED_I2C1.SDA, M2.SDA
  N9: U1.GPIO22, Componente2.SCL, OLED_I2C1.SCK, M2.SCL
  N10: R1.Pin_1, LED1.red_anode
  N11: R2.Pin_1, LED1.green_anode
  N12: R3.Pin_1, LED1.blue_anode

notes:
  RGB LED
  GPS
  Luminosidade
  Pressão
  Altitude
  Display OLED
  ESP32
  Temperatura
  Umidade

custom parts:
  ESP32-38PinWide: Generic 38-Pin ESP32 with wide format (only access to one side of pins on a breadboard) based on Stephen Lilley's HiLetgo ESP-WROOM-32 ESP32 ESP-32S Development Board.
  NEO-6M GPS Module: GY-GPS6MV2 NEO-6M GPS Module Module based on U-blox NEO-6M GPS engine, incorporating regulator for 3.3-5V DC input, MS621FE-compatible rechargeable battery for backup and EEPROM for storing configuration settings. Links: NEO-6 series product information page NEO-6 Datasheet
  BH1750: Light Sensor
  BME280: Temperature Humidity Barometric presure Sensor
